// Logisim project project1.circ as structural Verilog: 15 circuits, main circuit main
module main (
  input  [7:0] in_1,
  input  [7:0] in_2
);

  wire combinesignled_1_sign, combinesignled_2_sign, led16_1_ssign;
  wire [3:0] combinesignled_1_lsb, combinesignled_1_msb, combinesignled_1_out_4, combinesignled_2_lsb,
       combinesignled_2_msb, combinesignled_2_out_4, led16_1_lsb, led16_1_msb, led16_1_out_4, led16_1_out_5,
       led16_1_out_6;
  wire [15:0] boothimplement_1_out_3;

  CombineSignLED combinesignled_1 (
    .in_1(in_1), .sign(combinesignled_1_sign), .MSB(combinesignled_1_msb), .out_4(combinesignled_1_out_4),
    .lsb(combinesignled_1_lsb));
  CombineSignLED combinesignled_2 (
    .in_1(in_2), .sign(combinesignled_2_sign), .MSB(combinesignled_2_msb), .out_4(combinesignled_2_out_4),
    .lsb(combinesignled_2_lsb));
  _7_Segment_Display u_7_segment_display_1 (.g(combinesignled_1_sign));  // open: f, a, b, e, d, c, dp
  BoothImplement boothimplement_1 (.in_1(in_1), .in_2(in_2), .out_3(boothimplement_1_out_3));
  _7_Segment_Display u_7_segment_display_2 (.g(combinesignled_2_sign));  // open: f, a, b, e, d, c, dp
  Hex_Digit_Display hex_digit_display_1 (.value(combinesignled_1_msb));  // open: dp
  Led16 led16_1 (
    .in_1(boothimplement_1_out_3), .ssign(led16_1_ssign), .MSB(led16_1_msb), .out_4(led16_1_out_4),
    .out_5(led16_1_out_5), .out_6(led16_1_out_6), .lsb(led16_1_lsb));
  Hex_Digit_Display hex_digit_display_2 (.value(combinesignled_2_msb));  // open: dp
  Hex_Digit_Display hex_digit_display_3 (.value(combinesignled_1_out_4));  // open: dp
  Hex_Digit_Display hex_digit_display_4 (.value(combinesignled_1_lsb));  // open: dp
  Hex_Digit_Display hex_digit_display_5 (.value(combinesignled_2_out_4));  // open: dp
  Hex_Digit_Display hex_digit_display_6 (.value(combinesignled_2_lsb));  // open: dp
  _7_Segment_Display u_7_segment_display_3 (.g(led16_1_ssign));  // open: f, a, b, e, d, c, dp
  Hex_Digit_Display hex_digit_display_7 (.value(led16_1_msb));  // open: dp
  Hex_Digit_Display hex_digit_display_8 (.value(led16_1_out_5));  // open: dp
  Hex_Digit_Display hex_digit_display_9 (.value(led16_1_out_4));  // open: dp
  Hex_Digit_Display hex_digit_display_10 (.value(led16_1_out_6));  // open: dp
  Hex_Digit_Display hex_digit_display_11 (.value(led16_1_lsb));  // open: dp
endmodule

module FA (
  input  A,
  input  B,
  input  Cin,
  output Sum,
  output Cout
);

  wire and_1_out, and_2_out, xor_1_out;

  xor xor_1 (xor_1_out, A, B);
  and and_1 (and_1_out, B, A);
  and and_2 (and_2_out, Cin, xor_1_out);
  xor xor_2 (Sum, xor_1_out, Cin);
  or or_1 (Cout, and_1_out, and_2_out);
endmodule

// ckAdd
module checkbigger5andadd3 (
  input  msb,
  input  in_2,
  input  in_3,
  input  lsb,
  output out_5,
  output out_6,
  output out_7,
  output out_8
);

  wire and_1_out, and_2_out, or_1_out;
  wire [3:0] demultiplexer_1_out0, demultiplexer_1_out1, fa4bit_1_sum;

  Demultiplexer #(.width(4), .enable("false")) demultiplexer_1 (
    .out0(demultiplexer_1_out0), .out1(demultiplexer_1_out1), .in({msb, in_2, in_3, lsb}), .sel(or_1_out));
  FA4BIT fa4bit_1 (.A(demultiplexer_1_out1), .B(4'b0011), .Sum(fa4bit_1_sum));  // open: Cin, Cout
  and and_1 (and_1_out, in_2, in_3);
  and and_2 (and_2_out, in_2, lsb);
  or or_1 (or_1_out, msb, and_1_out, and_2_out);
  Multiplexer #(.width(4), .enable("false")) multiplexer_1 (
    .in0(demultiplexer_1_out0), .in1(fa4bit_1_sum), .out({out_5, out_6, out_7, out_8}), .sel(or_1_out));
endmodule

module FA4BIT (
  input  Cin,
  input  [3:0] A,
  input  [3:0] B,
  output [3:0] Sum,
  output Cout
);

  wire fa_1_cout, fa_2_cout, fa_3_cout;

  FA fa_1 (.A(A[0]), .B(B[0]), .Cin(Cin), .Sum(Sum[0]), .Cout(fa_1_cout));
  FA fa_2 (.A(A[1]), .B(B[1]), .Cin(fa_1_cout), .Sum(Sum[1]), .Cout(fa_2_cout));
  FA fa_3 (.A(A[2]), .B(B[2]), .Cin(fa_2_cout), .Sum(Sum[2]), .Cout(fa_3_cout));
  FA fa_4 (.A(A[3]), .B(B[3]), .Cin(fa_3_cout), .Sum(Sum[3]), .Cout(Cout));
endmodule

// bcd8
module L_7fb6cd38 (
  input  [7:0] in_1,
  output [3:0] out_2,
  output [3:0] out_3,
  output [3:0] out_4
);

  wire checkbigger5andadd3_1_out_5, checkbigger5andadd3_1_out_6, checkbigger5andadd3_1_out_7,
       checkbigger5andadd3_1_out_8, checkbigger5andadd3_2_out_5, checkbigger5andadd3_2_out_6,
       checkbigger5andadd3_2_out_7, checkbigger5andadd3_2_out_8, checkbigger5andadd3_3_out_5,
       checkbigger5andadd3_3_out_6, checkbigger5andadd3_3_out_7, checkbigger5andadd3_3_out_8,
       checkbigger5andadd3_4_out_5, checkbigger5andadd3_4_out_6, checkbigger5andadd3_4_out_7,
       checkbigger5andadd3_4_out_8, checkbigger5andadd3_5_out_6, checkbigger5andadd3_5_out_7,
       checkbigger5andadd3_5_out_8;

  checkbigger5andadd3 checkbigger5andadd3_1 (
    .msb(1'b0), .in_2(in_1[7]), .in_3(in_1[6]), .lsb(in_1[5]), .out_5(checkbigger5andadd3_1_out_5),
    .out_6(checkbigger5andadd3_1_out_6), .out_7(checkbigger5andadd3_1_out_7),
    .out_8(checkbigger5andadd3_1_out_8));
  checkbigger5andadd3 checkbigger5andadd3_2 (
    .msb(checkbigger5andadd3_1_out_6), .in_2(checkbigger5andadd3_1_out_7),
    .in_3(checkbigger5andadd3_1_out_8), .lsb(in_1[4]), .out_5(checkbigger5andadd3_2_out_5),
    .out_6(checkbigger5andadd3_2_out_6), .out_7(checkbigger5andadd3_2_out_7),
    .out_8(checkbigger5andadd3_2_out_8));
  checkbigger5andadd3 checkbigger5andadd3_3 (
    .msb(checkbigger5andadd3_2_out_6), .in_2(checkbigger5andadd3_2_out_7),
    .in_3(checkbigger5andadd3_2_out_8), .lsb(in_1[3]), .out_5(checkbigger5andadd3_3_out_5),
    .out_6(checkbigger5andadd3_3_out_6), .out_7(checkbigger5andadd3_3_out_7),
    .out_8(checkbigger5andadd3_3_out_8));
  checkbigger5andadd3 checkbigger5andadd3_4 (
    .msb(checkbigger5andadd3_3_out_6), .in_2(checkbigger5andadd3_3_out_7),
    .in_3(checkbigger5andadd3_3_out_8), .lsb(in_1[2]), .out_5(checkbigger5andadd3_4_out_5),
    .out_6(checkbigger5andadd3_4_out_6), .out_7(checkbigger5andadd3_4_out_7),
    .out_8(checkbigger5andadd3_4_out_8));
  checkbigger5andadd3 checkbigger5andadd3_5 (
    .msb(1'b0), .in_2(checkbigger5andadd3_1_out_5), .in_3(checkbigger5andadd3_2_out_5),
    .lsb(checkbigger5andadd3_3_out_5), .out_5(out_2[1]), .out_6(checkbigger5andadd3_5_out_6),
    .out_7(checkbigger5andadd3_5_out_7), .out_8(checkbigger5andadd3_5_out_8));
  checkbigger5andadd3 checkbigger5andadd3_6 (
    .msb(checkbigger5andadd3_5_out_6), .in_2(checkbigger5andadd3_5_out_7),
    .in_3(checkbigger5andadd3_5_out_8), .lsb(checkbigger5andadd3_4_out_5), .out_5(out_2[0]),
    .out_6(out_3[3]), .out_7(out_3[2]), .out_8(out_3[1]));
  checkbigger5andadd3 checkbigger5andadd3_7 (
    .msb(checkbigger5andadd3_4_out_6), .in_2(checkbigger5andadd3_4_out_7),
    .in_3(checkbigger5andadd3_4_out_8), .lsb(in_1[1]), .out_5(out_3[0]), .out_6(out_4[3]), .out_7(out_4[2]),
    .out_8(out_4[1]));

  assign out_2[3:2] = 2'b00;
  assign out_4[0] = in_1[0];
endmodule

// BCD8
module CombineSignLED (
  input  [7:0] in_1,
  output sign,
  output [3:0] MSB,
  output [3:0] out_4,
  output [3:0] lsb
);

  wire [7:0] complement8bit_1_cout;

  Complement8Bit complement8bit_1 (.Cin(in_1), .Enable(in_1[7]), .Cout(complement8bit_1_cout));
  L_7fb6cd38 l_7fb6cd38_1 (.in_1(complement8bit_1_cout), .out_2(MSB), .out_3(out_4), .out_4(lsb));

  assign sign = in_1[7];
endmodule

// FA8
module FA8BIT (
  input  Cin,
  input  [7:0] A,
  input  [7:0] B,
  output [7:0] sum,
  output cout
);

  wire fa4bit_1_cout;

  FA4BIT fa4bit_1 (.Cin(Cin), .A(A[3:0]), .B(B[3:0]), .Sum(sum[3:0]), .Cout(fa4bit_1_cout));
  FA4BIT fa4bit_2 (.Cin(fa4bit_1_cout), .A(A[7:4]), .B(B[7:4]), .Sum(sum[7:4]), .Cout(cout));
endmodule

// check
module Check2lastbit (
  input  q0,
  input  q1,
  output sign,
  output isdiff
);

  wire not_1_out;

  and and_1 (sign, not_1_out, q1);
  not not_1 (not_1_out, q0);
  xor xor_1 (isdiff, q0, q1);
endmodule

// Cell
module BoothCell (
  input  [7:0] Multiplicant,
  input  qn,
  input  [15:0] Q,
  output nextQn,
  output [15:0] AggrerateSum
);

  wire check2lastbit_1_isdiff, check2lastbit_1_sign;
  wire [7:0] complement8bit_1_cout, fa8bit_1_sum;

  Check2lastbit check2lastbit_1 (.q0(qn), .q1(Q[0]), .sign(check2lastbit_1_sign), .isdiff(check2lastbit_1_isdiff));
  Complement8Bit complement8bit_1 (.Cin(Multiplicant), .Enable(check2lastbit_1_sign), .Cout(complement8bit_1_cout));
  FA8BIT fa8bit_1 (.A(complement8bit_1_cout), .B(Q[15:8]), .sum(fa8bit_1_sum));  // open: Cin, cout
  Multiplexer #(.width(8), .enable("false")) multiplexer_1 (
    .in0(Q[15:8]), .in1(fa8bit_1_sum), .out({AggrerateSum[15], AggrerateSum[13:7]}),
    .sel(check2lastbit_1_isdiff));

  assign {AggrerateSum[14], AggrerateSum[6:0]} = {AggrerateSum[15], Q[7:1]};
  assign nextQn = Q[0];
endmodule

// Com8
module Complement8Bit (
  input  [7:0] Cin,
  input  Enable,
  output [7:0] Cout
);

  wire [7:0] demultiplexer_1_out0, demultiplexer_1_out1, fa8bit_1_sum, not_1_out;

  Demultiplexer #(.width(8), .enable("false")) demultiplexer_1 (
    .out0(demultiplexer_1_out0), .out1(demultiplexer_1_out1), .in(Cin), .sel(Enable));
  assign not_1_out = ~demultiplexer_1_out1;  // NOT_Gate not_1, 8 bits wide
  FA8BIT fa8bit_1 (.A(not_1_out), .B(8'h1), .sum(fa8bit_1_sum));  // open: Cin, cout
  Multiplexer #(.width(8), .enable("false")) multiplexer_1 (
    .in0(demultiplexer_1_out0), .in1(fa8bit_1_sum), .out(Cout), .sel(Enable));
endmodule

// Mul
module BoothImplement (
  input  [7:0] in_1,
  input  [7:0] in_2,
  output [15:0] out_3
);

  wire boothcell_1_nextqn, boothcell_2_nextqn, boothcell_3_nextqn, boothcell_4_nextqn, boothcell_5_nextqn,
       boothcell_6_nextqn, boothcell_7_nextqn;
  wire [15:0] boothcell_1_aggreratesum, boothcell_2_aggreratesum, boothcell_3_aggreratesum,
       boothcell_4_aggreratesum, boothcell_5_aggreratesum, boothcell_6_aggreratesum, boothcell_7_aggreratesum;

  BoothCell boothcell_1 (
    .Multiplicant(in_1), .Q({{8{1'b0}}, in_2}), .nextQn(boothcell_1_nextqn),
    .AggrerateSum(boothcell_1_aggreratesum));  // open: qn
  BoothCell boothcell_2 (
    .Multiplicant(in_1), .qn(boothcell_3_nextqn), .Q(boothcell_3_aggreratesum), .nextQn(boothcell_2_nextqn),
    .AggrerateSum(boothcell_2_aggreratesum));
  BoothCell boothcell_3 (
    .Multiplicant(in_1), .qn(boothcell_1_nextqn), .Q(boothcell_1_aggreratesum), .nextQn(boothcell_3_nextqn),
    .AggrerateSum(boothcell_3_aggreratesum));
  BoothCell boothcell_4 (
    .Multiplicant(in_1), .qn(boothcell_5_nextqn), .Q(boothcell_5_aggreratesum), .nextQn(boothcell_4_nextqn),
    .AggrerateSum(boothcell_4_aggreratesum));
  BoothCell boothcell_5 (
    .Multiplicant(in_1), .qn(boothcell_2_nextqn), .Q(boothcell_2_aggreratesum), .nextQn(boothcell_5_nextqn),
    .AggrerateSum(boothcell_5_aggreratesum));
  BoothCell boothcell_6 (
    .Multiplicant(in_1), .qn(boothcell_7_nextqn), .Q(boothcell_7_aggreratesum), .nextQn(boothcell_6_nextqn),
    .AggrerateSum(boothcell_6_aggreratesum));
  BoothCell boothcell_7 (
    .Multiplicant(in_1), .qn(boothcell_4_nextqn), .Q(boothcell_4_aggreratesum), .nextQn(boothcell_7_nextqn),
    .AggrerateSum(boothcell_7_aggreratesum));
  BoothCell boothcell_8 (
    .Multiplicant(in_1), .qn(boothcell_6_nextqn), .Q(boothcell_6_aggreratesum), .AggrerateSum(out_3));  // open: nextQn
endmodule

module binaryBCD16bit (
  input  [15:0] in_1,
  output [3:0] out_2,
  output [3:0] out_3,
  output [3:0] out_4,
  output [3:0] out_5,
  output [3:0] out_6
);

  wire checkbigger5andadd3_1_out_6, checkbigger5andadd3_1_out_7, checkbigger5andadd3_1_out_8,
       checkbigger5andadd3_2_out_5, checkbigger5andadd3_2_out_6, checkbigger5andadd3_2_out_7,
       checkbigger5andadd3_2_out_8, checkbigger5andadd3_3_out_5, checkbigger5andadd3_3_out_6,
       checkbigger5andadd3_3_out_7, checkbigger5andadd3_3_out_8, checkbigger5andadd3_4_out_5,
       checkbigger5andadd3_4_out_6, checkbigger5andadd3_4_out_7, checkbigger5andadd3_4_out_8,
       checkbigger5andadd3_5_out_5, checkbigger5andadd3_5_out_6, checkbigger5andadd3_5_out_7,
       checkbigger5andadd3_5_out_8, checkbigger5andadd3_6_out_5, checkbigger5andadd3_6_out_6,
       checkbigger5andadd3_6_out_7, checkbigger5andadd3_6_out_8, checkbigger5andadd3_7_out_5,
       checkbigger5andadd3_7_out_6, checkbigger5andadd3_7_out_7, checkbigger5andadd3_7_out_8,
       checkbigger5andadd3_8_out_5, checkbigger5andadd3_8_out_6, checkbigger5andadd3_8_out_7,
       checkbigger5andadd3_8_out_8, checkbigger5andadd3_9_out_5, checkbigger5andadd3_9_out_6,
       checkbigger5andadd3_9_out_7, checkbigger5andadd3_9_out_8, checkbigger5andadd3_10_out_6,
       checkbigger5andadd3_10_out_7, checkbigger5andadd3_10_out_8, checkbigger5andadd3_11_out_5,
       checkbigger5andadd3_11_out_6, checkbigger5andadd3_11_out_7, checkbigger5andadd3_11_out_8,
       checkbigger5andadd3_12_out_5, checkbigger5andadd3_12_out_6, checkbigger5andadd3_12_out_7,
       checkbigger5andadd3_12_out_8, checkbigger5andadd3_13_out_6, checkbigger5andadd3_13_out_7,
       checkbigger5andadd3_13_out_8, checkbigger5andadd3_16_out_5, checkbigger5andadd3_16_out_6,
       checkbigger5andadd3_16_out_7, checkbigger5andadd3_16_out_8, checkbigger5andadd3_17_out_5,
       checkbigger5andadd3_17_out_6, checkbigger5andadd3_17_out_7, checkbigger5andadd3_17_out_8,
       checkbigger5andadd3_18_out_5, checkbigger5andadd3_18_out_6, checkbigger5andadd3_18_out_7,
       checkbigger5andadd3_18_out_8, checkbigger5andadd3_19_out_5, checkbigger5andadd3_19_out_6,
       checkbigger5andadd3_19_out_7, checkbigger5andadd3_19_out_8, checkbigger5andadd3_20_out_5,
       checkbigger5andadd3_20_out_6, checkbigger5andadd3_20_out_7, checkbigger5andadd3_20_out_8,
       checkbigger5andadd3_21_out_5, checkbigger5andadd3_21_out_6, checkbigger5andadd3_21_out_7,
       checkbigger5andadd3_21_out_8, checkbigger5andadd3_22_out_5, checkbigger5andadd3_22_out_6,
       checkbigger5andadd3_22_out_7, checkbigger5andadd3_22_out_8, checkbigger5andadd3_23_out_5,
       checkbigger5andadd3_23_out_6, checkbigger5andadd3_23_out_7, checkbigger5andadd3_23_out_8;
  wire [3:0] l_7fb6cd38_1_out_2, l_7fb6cd38_1_out_3, l_7fb6cd38_1_out_4;

  checkbigger5andadd3 checkbigger5andadd3_1 (
    .msb(l_7fb6cd38_1_out_2[3]), .in_2(checkbigger5andadd3_3_out_5), .in_3(checkbigger5andadd3_4_out_5),
    .lsb(checkbigger5andadd3_7_out_5), .out_5(out_2[3]), .out_6(checkbigger5andadd3_1_out_6),
    .out_7(checkbigger5andadd3_1_out_7), .out_8(checkbigger5andadd3_1_out_8));
  checkbigger5andadd3 checkbigger5andadd3_2 (
    .msb(l_7fb6cd38_1_out_3[2]), .in_2(l_7fb6cd38_1_out_3[1]), .in_3(l_7fb6cd38_1_out_3[0]),
    .lsb(l_7fb6cd38_1_out_4[3]), .out_5(checkbigger5andadd3_2_out_5), .out_6(checkbigger5andadd3_2_out_6),
    .out_7(checkbigger5andadd3_2_out_7), .out_8(checkbigger5andadd3_2_out_8));
  checkbigger5andadd3 checkbigger5andadd3_3 (
    .msb(l_7fb6cd38_1_out_2[2]), .in_2(l_7fb6cd38_1_out_2[1]), .in_3(l_7fb6cd38_1_out_2[0]),
    .lsb(l_7fb6cd38_1_out_3[3]), .out_5(checkbigger5andadd3_3_out_5), .out_6(checkbigger5andadd3_3_out_6),
    .out_7(checkbigger5andadd3_3_out_7), .out_8(checkbigger5andadd3_3_out_8));
  checkbigger5andadd3 checkbigger5andadd3_4 (
    .msb(checkbigger5andadd3_3_out_6), .in_2(checkbigger5andadd3_3_out_7),
    .in_3(checkbigger5andadd3_3_out_8), .lsb(checkbigger5andadd3_2_out_5),
    .out_5(checkbigger5andadd3_4_out_5), .out_6(checkbigger5andadd3_4_out_6),
    .out_7(checkbigger5andadd3_4_out_7), .out_8(checkbigger5andadd3_4_out_8));
  checkbigger5andadd3 checkbigger5andadd3_5 (
    .msb(checkbigger5andadd3_2_out_6), .in_2(checkbigger5andadd3_2_out_7),
    .in_3(checkbigger5andadd3_2_out_8), .lsb(checkbigger5andadd3_16_out_5),
    .out_5(checkbigger5andadd3_5_out_5), .out_6(checkbigger5andadd3_5_out_6),
    .out_7(checkbigger5andadd3_5_out_7), .out_8(checkbigger5andadd3_5_out_8));
  checkbigger5andadd3 checkbigger5andadd3_6 (
    .msb(checkbigger5andadd3_5_out_6), .in_2(checkbigger5andadd3_5_out_7),
    .in_3(checkbigger5andadd3_5_out_8), .lsb(checkbigger5andadd3_17_out_5),
    .out_5(checkbigger5andadd3_6_out_5), .out_6(checkbigger5andadd3_6_out_6),
    .out_7(checkbigger5andadd3_6_out_7), .out_8(checkbigger5andadd3_6_out_8));
  checkbigger5andadd3 checkbigger5andadd3_7 (
    .msb(checkbigger5andadd3_4_out_6), .in_2(checkbigger5andadd3_4_out_7),
    .in_3(checkbigger5andadd3_4_out_8), .lsb(checkbigger5andadd3_5_out_5),
    .out_5(checkbigger5andadd3_7_out_5), .out_6(checkbigger5andadd3_7_out_6),
    .out_7(checkbigger5andadd3_7_out_7), .out_8(checkbigger5andadd3_7_out_8));
  checkbigger5andadd3 checkbigger5andadd3_8 (
    .msb(checkbigger5andadd3_7_out_6), .in_2(checkbigger5andadd3_7_out_7),
    .in_3(checkbigger5andadd3_7_out_8), .lsb(checkbigger5andadd3_6_out_5),
    .out_5(checkbigger5andadd3_8_out_5), .out_6(checkbigger5andadd3_8_out_6),
    .out_7(checkbigger5andadd3_8_out_7), .out_8(checkbigger5andadd3_8_out_8));
  checkbigger5andadd3 checkbigger5andadd3_9 (
    .msb(checkbigger5andadd3_6_out_6), .in_2(checkbigger5andadd3_6_out_7),
    .in_3(checkbigger5andadd3_6_out_8), .lsb(checkbigger5andadd3_18_out_5),
    .out_5(checkbigger5andadd3_9_out_5), .out_6(checkbigger5andadd3_9_out_6),
    .out_7(checkbigger5andadd3_9_out_7), .out_8(checkbigger5andadd3_9_out_8));
  checkbigger5andadd3 checkbigger5andadd3_10 (
    .msb(checkbigger5andadd3_1_out_6), .in_2(checkbigger5andadd3_1_out_7),
    .in_3(checkbigger5andadd3_1_out_8), .lsb(checkbigger5andadd3_8_out_5), .out_5(out_2[2]),
    .out_6(checkbigger5andadd3_10_out_6), .out_7(checkbigger5andadd3_10_out_7),
    .out_8(checkbigger5andadd3_10_out_8));
  checkbigger5andadd3 checkbigger5andadd3_11 (
    .msb(checkbigger5andadd3_8_out_6), .in_2(checkbigger5andadd3_8_out_7),
    .in_3(checkbigger5andadd3_8_out_8), .lsb(checkbigger5andadd3_9_out_5),
    .out_5(checkbigger5andadd3_11_out_5), .out_6(checkbigger5andadd3_11_out_6),
    .out_7(checkbigger5andadd3_11_out_7), .out_8(checkbigger5andadd3_11_out_8));
  checkbigger5andadd3 checkbigger5andadd3_12 (
    .msb(checkbigger5andadd3_11_out_6), .in_2(checkbigger5andadd3_11_out_7),
    .in_3(checkbigger5andadd3_11_out_8), .lsb(checkbigger5andadd3_21_out_5),
    .out_5(checkbigger5andadd3_12_out_5), .out_6(checkbigger5andadd3_12_out_6),
    .out_7(checkbigger5andadd3_12_out_7), .out_8(checkbigger5andadd3_12_out_8));
  checkbigger5andadd3 checkbigger5andadd3_13 (
    .msb(checkbigger5andadd3_10_out_6), .in_2(checkbigger5andadd3_10_out_7),
    .in_3(checkbigger5andadd3_10_out_8), .lsb(checkbigger5andadd3_11_out_5), .out_5(out_2[1]),
    .out_6(checkbigger5andadd3_13_out_6), .out_7(checkbigger5andadd3_13_out_7),
    .out_8(checkbigger5andadd3_13_out_8));
  checkbigger5andadd3 checkbigger5andadd3_14 (
    .msb(checkbigger5andadd3_13_out_6), .in_2(checkbigger5andadd3_13_out_7),
    .in_3(checkbigger5andadd3_13_out_8), .lsb(checkbigger5andadd3_12_out_5), .out_5(out_2[0]),
    .out_6(out_3[3]), .out_7(out_3[2]), .out_8(out_3[1]));
  checkbigger5andadd3 checkbigger5andadd3_15 (
    .msb(checkbigger5andadd3_12_out_6), .in_2(checkbigger5andadd3_12_out_7),
    .in_3(checkbigger5andadd3_12_out_8), .lsb(checkbigger5andadd3_23_out_5), .out_5(out_3[0]),
    .out_6(out_4[3]), .out_7(out_4[2]), .out_8(out_4[1]));
  L_7fb6cd38 l_7fb6cd38_1 (
    .in_1(in_1[15:8]), .out_2(l_7fb6cd38_1_out_2), .out_3(l_7fb6cd38_1_out_3), .out_4(l_7fb6cd38_1_out_4));
  checkbigger5andadd3 checkbigger5andadd3_16 (
    .msb(l_7fb6cd38_1_out_4[2]), .in_2(l_7fb6cd38_1_out_4[1]), .in_3(l_7fb6cd38_1_out_4[0]), .lsb(in_1[7]),
    .out_5(checkbigger5andadd3_16_out_5), .out_6(checkbigger5andadd3_16_out_6),
    .out_7(checkbigger5andadd3_16_out_7), .out_8(checkbigger5andadd3_16_out_8));
  checkbigger5andadd3 checkbigger5andadd3_17 (
    .msb(checkbigger5andadd3_16_out_6), .in_2(checkbigger5andadd3_16_out_7),
    .in_3(checkbigger5andadd3_16_out_8), .lsb(in_1[6]), .out_5(checkbigger5andadd3_17_out_5),
    .out_6(checkbigger5andadd3_17_out_6), .out_7(checkbigger5andadd3_17_out_7),
    .out_8(checkbigger5andadd3_17_out_8));
  checkbigger5andadd3 checkbigger5andadd3_18 (
    .msb(checkbigger5andadd3_17_out_6), .in_2(checkbigger5andadd3_17_out_7),
    .in_3(checkbigger5andadd3_17_out_8), .lsb(in_1[5]), .out_5(checkbigger5andadd3_18_out_5),
    .out_6(checkbigger5andadd3_18_out_6), .out_7(checkbigger5andadd3_18_out_7),
    .out_8(checkbigger5andadd3_18_out_8));
  checkbigger5andadd3 checkbigger5andadd3_19 (
    .msb(checkbigger5andadd3_18_out_6), .in_2(checkbigger5andadd3_18_out_7),
    .in_3(checkbigger5andadd3_18_out_8), .lsb(in_1[4]), .out_5(checkbigger5andadd3_19_out_5),
    .out_6(checkbigger5andadd3_19_out_6), .out_7(checkbigger5andadd3_19_out_7),
    .out_8(checkbigger5andadd3_19_out_8));
  checkbigger5andadd3 checkbigger5andadd3_20 (
    .msb(checkbigger5andadd3_19_out_6), .in_2(checkbigger5andadd3_19_out_7),
    .in_3(checkbigger5andadd3_19_out_8), .lsb(in_1[3]), .out_5(checkbigger5andadd3_20_out_5),
    .out_6(checkbigger5andadd3_20_out_6), .out_7(checkbigger5andadd3_20_out_7),
    .out_8(checkbigger5andadd3_20_out_8));
  checkbigger5andadd3 checkbigger5andadd3_21 (
    .msb(checkbigger5andadd3_9_out_6), .in_2(checkbigger5andadd3_9_out_7),
    .in_3(checkbigger5andadd3_9_out_8), .lsb(checkbigger5andadd3_19_out_5),
    .out_5(checkbigger5andadd3_21_out_5), .out_6(checkbigger5andadd3_21_out_6),
    .out_7(checkbigger5andadd3_21_out_7), .out_8(checkbigger5andadd3_21_out_8));
  checkbigger5andadd3 checkbigger5andadd3_22 (
    .msb(checkbigger5andadd3_20_out_6), .in_2(checkbigger5andadd3_20_out_7),
    .in_3(checkbigger5andadd3_20_out_8), .lsb(in_1[2]), .out_5(checkbigger5andadd3_22_out_5),
    .out_6(checkbigger5andadd3_22_out_6), .out_7(checkbigger5andadd3_22_out_7),
    .out_8(checkbigger5andadd3_22_out_8));
  checkbigger5andadd3 checkbigger5andadd3_23 (
    .msb(checkbigger5andadd3_21_out_6), .in_2(checkbigger5andadd3_21_out_7),
    .in_3(checkbigger5andadd3_21_out_8), .lsb(checkbigger5andadd3_20_out_5),
    .out_5(checkbigger5andadd3_23_out_5), .out_6(checkbigger5andadd3_23_out_6),
    .out_7(checkbigger5andadd3_23_out_7), .out_8(checkbigger5andadd3_23_out_8));
  checkbigger5andadd3 checkbigger5andadd3_24 (
    .msb(checkbigger5andadd3_23_out_6), .in_2(checkbigger5andadd3_23_out_7),
    .in_3(checkbigger5andadd3_23_out_8), .lsb(checkbigger5andadd3_22_out_5), .out_5(out_4[0]),
    .out_6(out_5[3]), .out_7(out_5[2]), .out_8(out_5[1]));
  checkbigger5andadd3 checkbigger5andadd3_25 (
    .msb(checkbigger5andadd3_22_out_6), .in_2(checkbigger5andadd3_22_out_7),
    .in_3(checkbigger5andadd3_22_out_8), .lsb(in_1[1]), .out_5(out_5[0]), .out_6(out_6[3]), .out_7(out_6[2]),
    .out_8(out_6[1]));

  assign out_6[0] = in_1[0];
endmodule

module Complement16bit (
  input  [15:0] Cin,
  input  Enable,
  output [15:0] Cout
);

  wire [15:0] demultiplexer_1_out0, demultiplexer_1_out1, fa16_1_sum, not_1_out;

  Demultiplexer #(.width(16), .enable("false")) demultiplexer_1 (
    .out0(demultiplexer_1_out0), .out1(demultiplexer_1_out1), .in(Cin), .sel(Enable));
  assign not_1_out = ~demultiplexer_1_out1;  // NOT_Gate not_1, 16 bits wide
  FA16 fa16_1 (.A(not_1_out), .B(16'h1), .sum(fa16_1_sum));  // open: Cin, cout
  Multiplexer #(.width(16), .enable("false")) multiplexer_1 (
    .in0(demultiplexer_1_out0), .in1(fa16_1_sum), .out(Cout), .sel(Enable));
endmodule

module FA16 (
  input  Cin,
  input  [15:0] A,
  input  [15:0] B,
  output [15:0] sum,
  output cout
);

  wire fa8bit_1_cout;

  FA8BIT fa8bit_1 (.Cin(Cin), .A(A[7:0]), .B(B[7:0]), .sum(sum[7:0]), .cout(fa8bit_1_cout));
  FA8BIT fa8bit_2 (.Cin(fa8bit_1_cout), .A(A[15:8]), .B(B[15:8]), .sum(sum[15:8]), .cout(cout));
endmodule

module Led16 (
  input  [15:0] in_1,
  output ssign,
  output [3:0] MSB,
  output [3:0] out_4,
  output [3:0] out_5,
  output [3:0] out_6,
  output [3:0] lsb
);

  wire [15:0] complement16bit_1_cout;

  Complement16bit complement16bit_1 (.Cin(in_1), .Enable(in_1[15]), .Cout(complement16bit_1_cout));
  binaryBCD16bit binarybcd16bit_1 (
    .in_1(complement16bit_1_cout), .out_2(MSB), .out_3(out_4), .out_4(out_5), .out_5(out_6), .out_6(lsb));

  assign ssign = in_1[15];
endmodule
